# Fritzing sketch autoBlinds (saved by Fritzing 0.9.4)
breadboards: 1

parts:
  Part1 = Arduino Nano (Rev3.0)
  M2 = BTS7960
  V1 = DC Power [voltage=12V]
  M3 = DC Motor

nets:
  N1: Part1.GND, M2.pin8
  N2: Part1.D5, M2.pin2
  N3: Part1.D6, M2.pin1
  N4: Part1.5V, M2.pin3, M2.pin4, M2.pin7
  N5: M2.pin9, M3.pin_2
  N6: M2.pin10, M3.pin_1
  N7: M2.pin11, V1.V+
  N8: M2.pin12, V1.V-

custom parts:
  BTS7960: BTS7960 43A Peak Power H-Bridge PWM Motor Driver
